# Fritzing sketch wiring (saved by Fritzing 0.9.4)

parts:
  MCU1 = Raspberry Pi Zero
  NEOPIXEL1 = Neopixel Strip -- White (60/m) [part_number=1138]
  J1 = Camdenboss CTB0158-5 [part_number=CTB0158-5 package=THT]

nets:
  N1: MCU1.pin_6, MCU1.pin_9, NEOPIXEL1.GND, J1.terminal_5
  N2: MCU1.pin_12, NEOPIXEL1.DI
  N3: NEOPIXEL1.+5V, J1.terminal_2

custom parts:
  Neopixel Strip -- White (60/m): Neopixel Strip, White, 60 pixels per meter.
